// Logisim project Komparator_Mod_3.circ as structural Verilog: 1 circuit, main circuit main
module main (
  input  MSB,
  input  LSB,
  input  MSB_2,
  input  LSB_2,
  input  MSB_3,
  input  LSB_3,
  input  MSB_4,
  input  LSB_4
);

  wire and_1_out, and_2_out, and_3_out, and_4_out, not_1_out, not_2_out, not_3_out, not_4_out, or_1_out,
       or_2_out, xor_1_out, xor_2_out, xor_3_out, xor_4_out;

  xor xor_1 (xor_1_out, MSB, MSB_2);
  or or_1 (or_1_out, xor_1_out, xor_2_out);
  LED led_1 (.in(or_1_out));
  xor xor_2 (xor_2_out, LSB, LSB_2);
  not not_1 (not_1_out, LSB_4);
  and and_1 (and_1_out, not_1_out, MSB_4);
  xor xor_3 (xor_3_out, and_1_out, and_2_out);
  not not_2 (not_2_out, LSB_3);
  and and_2 (and_2_out, not_2_out, MSB_3);
  not not_3 (not_3_out, MSB_3);
  and and_3 (and_3_out, not_3_out, LSB_3);
  or or_2 (or_2_out, xor_3_out, xor_4_out);
  LED led_2 (.in(or_2_out));
  not not_4 (not_4_out, MSB_4);
  and and_4 (and_4_out, not_4_out, LSB_4);
  xor xor_4 (xor_4_out, and_3_out, and_4_out);

  // Notes on the sheet:
  //   Porównuje MSB
  //   |Z|
  //   Z
  //   Porównuje LSB
  //   |Z|
  //   Z
  //   <- Sygnał błędu wysyłany, gdy 2 sygnały porównywane do siebie się różnią
endmodule
