// Logisim project SumatorKaskadowy.circ as structural Verilog: 1 circuit, main circuit main
module main (
  input  cin,
  input  [3:0] A,
  input  [3:0] B,
  output [3:0] out_4,
  output out_5
);

  wire and_1_out, and_2_out, and_3_out, and_4_out, and_5_out, and_6_out, and_7_out, and_8_out, or_1_out,
       or_2_out, or_3_out, xor_1_out, xor_3_out, xor_5_out, xor_7_out;

  xor xor_1 (xor_1_out, A[0], B[0]);
  and and_1 (and_1_out, A[0], B[0]);
  xor xor_2 (out_4[0], cin, xor_1_out);
  and and_2 (and_2_out, xor_1_out, cin);
  or or_1 (or_1_out, and_2_out, and_1_out);
  xor xor_3 (xor_3_out, A[1], B[1]);
  and and_3 (and_3_out, A[1], B[1]);
  and and_4 (and_4_out, xor_3_out, or_1_out);
  xor xor_4 (out_4[1], or_1_out, xor_3_out);
  or or_2 (or_2_out, and_4_out, and_3_out);
  xor xor_5 (xor_5_out, A[2], B[2]);
  and and_5 (and_5_out, A[2], B[2]);
  xor xor_6 (out_4[2], or_2_out, xor_5_out);
  and and_6 (and_6_out, xor_5_out, or_2_out);
  or or_3 (or_3_out, and_6_out, and_5_out);
  xor xor_7 (xor_7_out, A[3], B[3]);
  and and_7 (and_7_out, A[3], B[3]);
  xor xor_8 (out_4[3], or_3_out, xor_7_out);
  and and_8 (and_8_out, xor_7_out, or_3_out);
  or or_4 (out_5, and_8_out, and_7_out);

  // Notes on the sheet:
  //   B0
  //   A0
  //   S0
  //   B1
  //   A1
  //   S1
  //   A2
  //   B2
  //   S2
  //   A3
  //   B3
  //   S3
  //   cout
  //   Suma
endmodule
