// Logisim project SumatorMod3.circ as structural Verilog: 1 circuit, main circuit main
module main (
  input  [1:0] mod_X,
  input  [1:0] mod_Y,
  output Z0,
  output Z1
);

  wire and_1_out, and_2_out, and_3_out, and_4_out, not_1_out, not_2_out, not_3_out, or_1_out, xor_1_out,
       xor_2_out, xor_3_out;

  not not_1 (not_1_out, mod_X[1]);
  not not_2 (not_2_out, mod_Y[1]);
  xor xor_1 (xor_1_out, mod_X[0], not_1_out);
  and and_1 (and_1_out, mod_X[0], not_1_out);
  xor xor_2 (xor_2_out, xor_1_out, mod_Y[0]);
  and and_2 (and_2_out, xor_1_out, mod_Y[0]);
  or or_1 (or_1_out, and_2_out, and_1_out);
  not not_3 (not_3_out, or_1_out);
  and and_3 (and_3_out, xor_2_out, not_3_out);
  xor xor_3 (xor_3_out, xor_2_out, not_3_out);
  xor xor_4 (Z0, xor_3_out, not_2_out);
  and and_4 (and_4_out, xor_3_out, not_2_out);
  or or_2 (Z1, and_4_out, and_3_out);

  // Notes on the sheet:
  //   SUMATOR MOD 3
endmodule
