// Logisim project backwards_error_detection_diagram_general.circ as structural Verilog: 1 circuit, main circuit main
module main (
  input  [3:0] in_1,
  input  [3:0] in_2,
  input  [3:0] Modulo_A,
  input  [3:0] in_4,
  input  [3:0] in_5,
  output [3:0] Z,
  output [3:0] out_7,
  output [3:0] X,
  output [3:0] Y,
  output [3:0] out_10
);

  wire comparator_1_gt, comparator_1_lt, or_1_out;
  wire [3:0] adder_2_out;

  Divider #(.width(4)) divider_1 (.a(in_1), .b(Modulo_A), .rem(X));  // open: out, upper
  Divider #(.width(4)) divider_2 (.a(in_2), .b(Modulo_A), .rem(Y));  // open: out, upper
  Adder #(.width(4)) adder_1 (.a(in_1), .b(in_2), .out(Z));  // open: cin, cout
  Adder #(.width(4)) adder_2 (.a(X), .b(Y), .out(adder_2_out));  // open: cin, cout
  Multiplexer multiplexer_1 ();  // open: in0, in1, out, sel
  Divider #(.width(4)) divider_3 (.a(adder_2_out), .b(in_4), .rem(out_7));  // open: out, upper
  Divider #(.width(4)) divider_4 (.a(Z), .b(in_5), .rem(out_10));  // open: out, upper
  Comparator #(.width(4)) comparator_1 (.a(out_10), .b(out_7), .gt(comparator_1_gt), .lt(comparator_1_lt));  // open: eq
  or or_1 (or_1_out, comparator_1_gt, comparator_1_lt);
  LED led_1 (.in(or_1_out));

  // Notes on the sheet:
  //   X
  //   Y
  //   Układy arytmetyczny
  //   Układ arytmetyczny
  //   Generator Resztowy
  //   mod A
  //   Komparator
  //   |Z|
  //   Sygnał błędu
endmodule
