// Logisim project genresztmod3_togit.circ as structural Verilog: 4 circuits, main circuit main
module main (
  input  [4:0] in_1,
  input  [5:0] in_2
);

  wire and_1_out, and_2_out, and_3_out, and_4_out, and_5_out, and_6_out, and_7_out, and_8_out, and_9_out,
       and_10_out, and_11_out, and_12_out, and_13_out, and_14_out, and_15_out, and_16_out, and_17_out,
       not_1_out, not_2_out, not_3_out, not_4_out, not_5_out, not_6_out, not_7_out, not_8_out, not_9_out,
       not_10_out, not_11_out, not_12_out, not_13_out, not_14_out, or_1_out, or_2_out, or_3_out, or_4_out,
       or_5_out, or_6_out, or_7_out, xor_1_out, xor_2_out, xor_3_out, xor_4_out, xor_5_out, xor_6_out,
       xor_7_out, xor_8_out, xor_9_out, xor_10_out, xor_11_out, xor_12_out, xor_13_out, xor_14_out,
       xor_15_out;

  not not_1 (not_1_out, in_2[5]);
  not not_2 (not_2_out, in_1[1]);
  not not_3 (not_3_out, in_1[3]);
  not not_4 (not_4_out, in_2[1]);
  not not_5 (not_5_out, in_2[3]);
  xor xor_1 (xor_1_out, in_1[0], not_2_out);
  and and_1 (and_1_out, in_1[0], not_2_out);
  xor xor_2 (xor_2_out, in_2[0], not_4_out);
  and and_2 (and_2_out, in_2[0], not_4_out);
  xor xor_3 (xor_3_out, not_5_out, in_2[4]);
  and and_3 (and_3_out, not_5_out, in_2[4]);
  xor xor_4 (xor_4_out, xor_1_out, in_1[2]);
  and and_4 (and_4_out, xor_1_out, in_1[2]);
  or or_1 (or_1_out, and_4_out, and_1_out);
  and and_5 (and_5_out, xor_2_out, in_2[2]);
  and and_6 (and_6_out, xor_3_out, not_1_out);
  not not_6 (not_6_out, or_1_out);
  xor xor_5 (xor_5_out, xor_2_out, in_2[2]);
  or or_2 (or_2_out, and_5_out, and_2_out);
  xor xor_6 (xor_6_out, xor_3_out, not_1_out);
  or or_3 (or_3_out, and_6_out, and_3_out);
  not not_7 (not_7_out, or_2_out);
  not not_8 (not_8_out, or_3_out);
  and and_7 (and_7_out, xor_4_out, not_6_out);
  xor xor_7 (xor_7_out, xor_4_out, not_6_out);
  xor xor_8 (xor_8_out, xor_5_out, not_7_out);
  and and_8 (and_8_out, xor_5_out, not_7_out);
  xor xor_9 (xor_9_out, xor_7_out, not_3_out);
  and and_9 (and_9_out, xor_7_out, not_3_out);
  or or_4 (or_4_out, and_9_out, and_7_out);
  and and_10 (and_10_out, xor_8_out, xor_6_out);
  not not_9 (not_9_out, or_4_out);
  xor xor_10 (xor_10_out, xor_8_out, xor_6_out);
  or or_5 (or_5_out, and_10_out, and_8_out);
  not not_10 (not_10_out, or_5_out);
  xor xor_11 (xor_11_out, xor_9_out, not_9_out);
  and and_11 (and_11_out, xor_9_out, not_9_out);
  xor xor_12 (xor_12_out, xor_10_out, not_10_out);
  and and_12 (and_12_out, xor_10_out, not_10_out);
  xor xor_13 (xor_13_out, xor_11_out, in_1[4]);
  and and_13 (and_13_out, xor_11_out, in_1[4]);
  or or_6 (or_6_out, and_13_out, and_11_out);
  and and_14 (and_14_out, xor_12_out, not_8_out);
  xor xor_14 (xor_14_out, xor_12_out, not_8_out);
  or or_7 (or_7_out, and_14_out, and_12_out);
  not not_11 (not_11_out, xor_13_out);
  and and_15 (and_15_out, not_11_out, or_6_out);
  xor xor_15 (xor_15_out, xor_13_out, or_6_out);
  LED Z0 (.in(and_15_out));
  not not_12 (not_12_out, xor_15_out);
  LED Z1 (.in(not_12_out));
  not not_13 (not_13_out, or_7_out);
  not not_14 (not_14_out, xor_14_out);
  and and_16 (and_16_out, xor_14_out, not_13_out);
  LED led_1 (.in(and_16_out));
  and and_17 (and_17_out, not_14_out, or_7_out);
  LED led_2 (.in(and_17_out));

  // Notes on the sheet:
  //   Z
  //   Z
  //   DLA n = 2k
  //   DLA n = 2k + 1
  //   Z0
  //   Z1
endmodule

module FullAdder (
  input  A,
  input  B,
  input  C_in,
  output S,
  output C_out
);

  wire and_1_out, and_2_out, xor_1_out;

  xor xor_1 (xor_1_out, A, B);
  and and_1 (and_1_out, A, B);
  xor xor_2 (S, xor_1_out, C_in);
  and and_2 (and_2_out, xor_1_out, C_in);
  or or_1 (C_out, and_2_out, and_1_out);
endmodule

module WyjscieDlaNieparzystejN (
  input  Sout_2kplus1n,
  input  Cout,
  output S0,
  output S1
);

  wire not_1_out, xor_1_out;

  not not_1 (not_1_out, Sout_2kplus1n);
  xor xor_1 (xor_1_out, Sout_2kplus1n, Cout);
  and and_1 (S0, not_1_out, Cout);
  not not_2 (S1, xor_1_out);
endmodule

module WyjscieDlaParzystejN (
  input  Sout_2kn,
  input  Cout,
  output S0,
  output S1
);

  wire not_1_out, not_2_out;

  not not_1 (not_1_out, Cout);
  not not_2 (not_2_out, Sout_2kn);
  and and_1 (S0, Sout_2kn, not_1_out);
  and and_2 (S1, not_2_out, Cout);
endmodule
